// Logisim project hw4.circ as structural Verilog
module RegisterFile (
  input  [2:0] WriteReg,
  input  [15:0] WriteData,
  input  [2:0] ReadReg1,
  input  [2:0] ReadReg2,
  input  RegWriteEnable,
  input  Reset,
  input  Clock,
  output [15:0] ReadData1,
  output [15:0] ReadData2
);

  wire and_1_out, and_2_out, and_3_out, and_4_out, and_5_out, and_6_out, and_7_out, and_8_out,
       decoder_1_out0, decoder_1_out1, decoder_1_out2, decoder_1_out3, decoder_1_out4, decoder_1_out5,
       decoder_1_out6, decoder_1_out7;
  wire [15:0] register_1_q, register_2_q, register_3_q, register_4_q, register_5_q, register_6_q,
       register_7_q, register_8_q;

  Decoder #(.select(3), .enable("false")) decoder_1 (
    .out0(decoder_1_out0), .out1(decoder_1_out1), .out2(decoder_1_out2), .out3(decoder_1_out3),
    .out4(decoder_1_out4), .out5(decoder_1_out5), .out6(decoder_1_out6), .out7(decoder_1_out7), .sel(WriteReg));
  and and_1 (and_1_out, decoder_1_out0, RegWriteEnable);
  and and_2 (and_2_out, decoder_1_out1, RegWriteEnable);
  and and_3 (and_3_out, decoder_1_out2, RegWriteEnable);
  and and_4 (and_4_out, decoder_1_out3, RegWriteEnable);
  and and_5 (and_5_out, decoder_1_out4, RegWriteEnable);
  and and_6 (and_6_out, decoder_1_out5, RegWriteEnable);
  and and_7 (and_7_out, decoder_1_out6, RegWriteEnable);
  and and_8 (and_8_out, decoder_1_out7, RegWriteEnable);
  // Probe on register_1_q
  Register #(.width(16), .trigger("falling")) register_1 (
    .D(WriteData), .en(and_1_out), .Q(register_1_q), .clk(Clock), .clr(Reset));
  // Probe on register_2_q
  Register #(.width(16), .trigger("falling")) register_2 (
    .D(WriteData), .en(and_2_out), .Q(register_2_q), .clk(Clock), .clr(Reset));
  // Probe on register_3_q
  Register #(.width(16), .trigger("falling")) register_3 (
    .D(WriteData), .en(and_3_out), .Q(register_3_q), .clk(Clock), .clr(Reset));
  // Probe on register_4_q
  Register #(.width(16), .trigger("falling")) register_4 (
    .D(WriteData), .en(and_4_out), .Q(register_4_q), .clk(Clock), .clr(Reset));
  // Probe on register_5_q
  Register #(.width(16), .trigger("falling")) register_5 (
    .D(WriteData), .en(and_5_out), .Q(register_5_q), .clk(Clock), .clr(Reset));
  // Probe on register_6_q
  Register #(.width(16), .trigger("falling")) register_6 (
    .D(WriteData), .en(and_6_out), .Q(register_6_q), .clk(Clock), .clr(Reset));
  // Probe on register_7_q
  Register #(.width(16), .trigger("falling")) register_7 (
    .D(WriteData), .en(and_7_out), .Q(register_7_q), .clk(Clock), .clr(Reset));
  // Probe on register_8_q
  Register #(.width(16), .trigger("falling")) register_8 (
    .D(WriteData), .en(and_8_out), .Q(register_8_q), .clk(Clock), .clr(Reset));
  Multiplexer #(.select(3), .width(16), .enable("false")) multiplexer_1 (
    .in0(register_1_q), .in1(register_2_q), .in2(register_3_q), .in3(register_4_q), .in4(register_5_q),
    .in5(register_6_q), .in6(register_7_q), .in7(register_8_q), .out(ReadData1), .sel(ReadReg1));
  Multiplexer #(.select(3), .width(16), .enable("false")) multiplexer_2 (
    .in0(register_1_q), .in1(register_2_q), .in2(register_3_q), .in3(register_4_q), .in4(register_5_q),
    .in5(register_6_q), .in6(register_7_q), .in7(register_8_q), .out(ReadData2), .sel(ReadReg2));

  // Other names for the same wires on the sheet: clk = Clock; data[15:0] = WriteData; R1[2:0] = ReadReg1;
  //   R2[2:0] = ReadReg2; WE = RegWriteEnable
endmodule
